# Fritzing sketch Bot (saved by Fritzing 0.6.3b)
breadboards: 1

parts:
  IC1 = H-Bridge [package=THT]
  J2 = female pin header, 4 pins [form="♀ (female)"]
  J3 = female pin header, 3 pins [form="♀ (female)"]
  J4 = female pin header, 3 pins [form="♀ (female)"]
  J1 = female pin header, 3 pins [form="♀ (female)"]

nets:
  N1: IC1.1_2EN, J3.pin3
  N2: IC1.1A, J3.pin2
  N3: IC1.1Y, J3.pin1
  GND: IC1.GND1, IC1.GND2, IC1.GND3, IC1.GND4, J1.pin3
  N4: IC1.2Y, J4.pin3
  N5: IC1.2A, J4.pin2
  N6: IC1.VCC2, J1.pin2
  N7: IC1.3_4EN, J4.pin1
  N8: IC1.3A, J2.pin4
  N9: IC1.3Y, J2.pin3
  N10: IC1.4Y, J2.pin2
  N11: IC1.4A, J2.pin1
  N12: IC1.VCC1, J1.pin1
